# Fritzing sketch CSNEA (saved by Fritzing 1.0.5)
breadboards: 1

parts:
  Part1 = Arduino Mega 2560 (Rev3)
  Part2 = Bluetooth HC-05 Macho
  DFRobot_DFPlayer_Mini1 = DFRobot DFPlayer Mini [part_number=DFR0299]
  R4 = Resistor [tolerance=±5% power=0.25W resistance=2k package=THT]
  R3 = Resistor [tolerance=±5% power=0.25W resistance=1k package=THT]
  R5 = Resistor [tolerance=±5% power=0.25W resistance=1k package=THT]
  SP1 = SPEAKER [package=pcb_mount_speaker]
  HC-SR04_Sensor_1 = HC-SR04 Ultrasonic Distance Sensor
  U1 = MAX7219 [package=dil24]  # not connected
  Disp1 = 32mm 8x8 dot matrix column cathode led display with standard pcb pads  # not connected
  Disp2 = 32mm 8x8 dot matrix row cathode led display with standard pcb pads  # not connected

nets:
  N1: Part1.D19/RX1, Part2.TXD
  N2: Part1.D18/TX1, R3.Pin_1
  N3: Part1.D17_PWM/RX2, DFRobot_DFPlayer_Mini1.TX
  N4: Part1.D16_PWM/TX2, R5.Pin_1
  GND: Part1.GND, Part2.GND, DFRobot_DFPlayer_Mini1.GND-1, DFRobot_DFPlayer_Mini1.GND-2, R4.Pin_1, HC-SR04_Sensor_1.GND
  VCC: Part1.5V, Part2.VCC, DFRobot_DFPlayer_Mini1.VCC, HC-SR04_Sensor_1.VCC
  N5: Part1.D41, Part2.State
  N6: Part1.D42, HC-SR04_Sensor_1.TRIG
  N7: Part1.D44, HC-SR04_Sensor_1.ECHO
  N8: Part2.RXD, R4.Pin_0, R3.Pin_0
  N9: DFRobot_DFPlayer_Mini1.RX, R5.Pin_0
  N10: DFRobot_DFPlayer_Mini1.SPK_1, SP1.+
  N11: DFRobot_DFPlayer_Mini1.SPK_2, SP1.-
