# Fritzing sketch CSNEA (saved by Fritzing 1.0.5)
# 18650 Li-ion Battery: CC-BY Dr Kristofer Chan, King's College London/Remote-research.org
circuit board: 33.6924cm x 18.523cm
breadboards: 1

parts:
  Arduino_Mega = Arduino Mega 2560 (Rev3)
  HC-05_Bluetooth_Module = Bluetooth HC-05 Macho
  DFPlayerMini = DFRobot DFPlayer Mini [part_number=DFR0299]
  R2_-_HC→GND = Resistor [tolerance=±5% power=0.25W resistance=2k package=THT]
  R1_-_TX1→HC = Resistor [tolerance=±5% power=0.25W resistance=1k package=THT]
  R3_-_TX2→DF = Resistor [tolerance=±5% power=0.25W resistance=1k package=THT]
  Speaker = SPEAKER [package=pcb_mount_speaker]
  HC-SR04_Distance_Sensor = HC-SR04 Ultrasonic Distance Sensor
  U1 = MAX7219 [package=dil24]  # not connected
  Disp1 = 32mm 8x8 dot matrix column cathode led display with standard pcb pads  # not connected
  Disp2 = 32mm 8x8 dot matrix row cathode led display with standard pcb pads  # not connected
  L298N_Motor_Controller = L298N DC motor driver
  Motor_FrontRight = DC Motor [voltage_(max)=6V voltage_(min)=3V]
  Motor_BackRight = DC Motor [voltage_(max)=6V voltage_(min)=3V]
  Motor_BackLeft = DC Motor [voltage_(max)=6V voltage_(min)=3V]
  Motor_FrontLeft = DC Motor [voltage_(max)=6V voltage_(min)=3V]
  U2 = MAX1555 Lithium Charger IC [package=sot23-5]  # not connected
  Li-ion_battery_1 = 18650 Li-ion Battery [package=battery-18650]
  Li-ion_battery_2 = 18650 Li-ion Battery [package=battery-18650]
  M5 = fc-51 [package=THT]  # not connected
  M6 = fc-51 [package=THT]  # not connected
  R4_-_DF→GND = Resistor [tolerance=±5% power=0.25W resistance=2k package=THT]
  IR_Reciever = KY-022 Infrared Receiver Module [package="Breakout board"]

nets:
  N1: Arduino_Mega.D19/RX1, HC-05_Bluetooth_Module.TXD
  N2: Arduino_Mega.D18/TX1, R1_-_TX1→HC.Pin_1
  N3: Arduino_Mega.D17_PWM/RX2, DFPlayerMini.TX
  N4: Arduino_Mega.D16_PWM/TX2, R3_-_TX2→DF.Pin_1, R4_-_DF→GND.Pin_0
  N5: Arduino_Mega.D11_PWM, IR_Reciever.S
  VCC: Arduino_Mega.5V, HC-05_Bluetooth_Module.VCC, DFPlayerMini.VCC, HC-SR04_Distance_Sensor.VCC, L298N_Motor_Controller.5V, L298N_Motor_Controller.+5V-J2, IR_Reciever.Vin
  GND: Arduino_Mega.GND, HC-05_Bluetooth_Module.GND, DFPlayerMini.GND-1, DFPlayerMini.GND-2, R2_-_HC→GND.Pin_1, HC-SR04_Distance_Sensor.GND, L298N_Motor_Controller.GND, Li-ion_battery_1.-, R4_-_DF→GND.Pin_1, IR_Reciever.-
  N6: Arduino_Mega.D41, HC-05_Bluetooth_Module.State
  N7: Arduino_Mega.D42, HC-SR04_Distance_Sensor.TRIG
  N8: Arduino_Mega.D43, L298N_Motor_Controller.ENB
  N9: Arduino_Mega.D44, HC-SR04_Distance_Sensor.ECHO
  N10: Arduino_Mega.D45, L298N_Motor_Controller.IN4
  N11: Arduino_Mega.D47, L298N_Motor_Controller.IN3
  N12: Arduino_Mega.D49, L298N_Motor_Controller.IN2
  N13: Arduino_Mega.D51, L298N_Motor_Controller.IN1
  N14: Arduino_Mega.D53, L298N_Motor_Controller.ENA
  N15: HC-05_Bluetooth_Module.RXD, R2_-_HC→GND.Pin_0, R1_-_TX1→HC.Pin_0
  N16: DFPlayerMini.RX, R3_-_TX2→DF.Pin_0
  N17: DFPlayerMini.SPK_1, Speaker.+
  N18: DFPlayerMini.SPK_2, Speaker.-
  N19: L298N_Motor_Controller.OUT1, Motor_BackRight.pin_2
  N20: L298N_Motor_Controller.OUT2, Motor_FrontRight.pin_1
  N21: L298N_Motor_Controller.12V, Li-ion_battery_2.+
  N22: L298N_Motor_Controller.OUT3, Motor_FrontLeft.pin_2
  N23: L298N_Motor_Controller.OUT4, Motor_BackLeft.pin_1
  N24: Motor_FrontRight.pin_2, Motor_BackRight.pin_1
  N25: Motor_BackLeft.pin_2, Motor_FrontLeft.pin_1
  N26: Li-ion_battery_1.+, Li-ion_battery_2.-

notes:
  stuff 2 be added here

custom parts:
  L298N DC motor driver: This L298N Motor Driver Module is a high power motor driver module for driving DC and Stepper Motors. This module consists of an L298 motor driver IC and a 78M05 5V regulator.
  18650 Li-ion Battery: 18650 li-ion Battery Standard 18650 battery with interactive connectors Creative Common Attribution 4.0 International (CC-BY 4.0) license. Any use of this part requires attribution of Dr Kristofer Chan, Department of Geography, King's College London. Contact kristofer.chan [at] kcl.ac.uk OR kris [at] remote-research.org for further information.
  KY-022 Infrared Receiver Module: KY-022 IR receiver module, reacts to 38kHz infrared light.
